// Logisim project ControlUnit.circ as structural Verilog: 1 circuit, main circuit main
module main (
  input  [3:0] Opcode,
  input  [2:0] Func,
  output RegDst,
  output RegWrite,
  output ALUSrc,
  output Beq,
  output J,
  output JAL,
  output JR,
  output [2:0] AluOp,
  output MemWrite,
  output MemRead,
  output MemtoReg,
  output ExLb,
  output LworLb,
  output storeReg
);

  wire ADDI, ANDI, Lbu, LUI_out, LW, LWS_out, or_4_out, Ori, sw;

  and LWS (LWS_out, Func[2], ~Func[1], ~Func[0], RegDst);  // AND_Gate
  and RType (RegDst, ~Opcode[3], ~Opcode[2], ~Opcode[1], ~Opcode[0]);  // AND_Gate
  and u_SW (sw, ~Opcode[3], Opcode[2], Opcode[1], Opcode[0]);  // AND_Gate
  and Sb (storeReg, Opcode[3], ~Opcode[2], ~Opcode[1], ~Opcode[0]);  // AND_Gate
  and u_LW (LW, ~Opcode[3], Opcode[2], ~Opcode[1], ~Opcode[0]);  // AND_Gate
  and u_Lbu (Lbu, ~Opcode[3], Opcode[2], ~Opcode[1], Opcode[0]);  // AND_Gate
  and Lb (ExLb, ~Opcode[3], Opcode[2], Opcode[1], ~Opcode[0]);  // AND_Gate
  and u_BEQ (Beq, Opcode[3], ~Opcode[2], ~Opcode[1], Opcode[0]);  // AND_Gate
  and u_J (J, Opcode[3], ~Opcode[2], Opcode[1], ~Opcode[0]);  // AND_Gate
  and u_JAL (JAL, Opcode[3], ~Opcode[2], Opcode[1], Opcode[0]);  // AND_Gate
  and LUI (LUI_out, Opcode[3], Opcode[2], ~Opcode[1], ~Opcode[0]);  // AND_Gate
  and u_ADDI (ADDI, ~Opcode[3], ~Opcode[2], Opcode[1], Opcode[0]);  // AND_Gate
  and u_ORI (Ori, ~Opcode[3], ~Opcode[2], Opcode[1], ~Opcode[0]);  // AND_Gate
  nor nor_1 (RegWrite, LUI_out, JAL, J, Beq, storeReg, sw);
  nor nor_2 (ALUSrc, RegDst, Beq);
  and and_1 (JR, RegDst, ~Func[0], ~Func[1], ~Func[2]);  // AND_Gate
  or or_1 (MemWrite, storeReg, sw);
  and u_ANDI (ANDI, ~Opcode[3], ~Opcode[2], ~Opcode[1], Opcode[0]);  // AND_Gate
  or or_2 (MemRead, LWS_out, ExLb, Lbu, LW);
  or or_3 (LworLb, ExLb, Lbu);
  assign AluOp = or_4_out ? 3'b011 : 3'bz;  // Controlled_Buffer controlled_buffer_1
  or or_4 (or_4_out, ADDI, LW, Lbu, ExLb, storeReg, sw);
  assign AluOp = RegDst ? Func : 3'bz;  // Controlled_Buffer controlled_buffer_2
  assign AluOp = Beq ? 3'b010 : 3'bz;  // Controlled_Buffer controlled_buffer_3
  assign AluOp = Ori ? 3'b110 : 3'bz;  // Controlled_Buffer controlled_buffer_4
  assign AluOp = ANDI ? 3'b111 : 3'bz;  // Controlled_Buffer controlled_buffer_5

  assign MemtoReg = MemRead;

  // Other names for the same wires on the sheet: Lb = ExLb; RType = RegDst; Sb = storeReg

  // Notes on the sheet:
  //   Add
  //   Sub
  //   Or
  //   And
endmodule
