// Logisim project DataPath.circ as structural Verilog
module main (
);

  wire AluSrc, AluSrcEX, BEQ, BEQ_EX, BEQ_MEM, carryOut, clk, extLb, extLb_EX, extLb_MEM, extLb_WB, J, J_Ex,
       J_MEM, JAL, JAL_EX, JAL_MEM, JR, JR_EX, JR_MEM, LwOrLb, LwOrLb_EX, LwOrLb_MEM, LwOrLb_WB, MemRead,
       MemRead_EX, MemRead_MEM, MemToReg, MemToReg_EX, MemToReg_MEM, MemToReg_WB, MemWrite, MemWrite_EX,
       MemWrite_MEM, not_1_out, not_2_out, PcSrc, regDst, regDst_EX, regDst_MEM, regWrite, regWrite_EX,
       regWrite_MEM, regWrite_WB, stall, StoreReg, StoreReg_EX, StoreReg_MEM, undriven, Zero_EX, Zero_MEM;
  wire [1:0] Forward_A, Forward_B;
  wire [2:0] AluOp, AluOpEX, EX_MEM_Rd, EX_MEM_Rs, EX_MEM_Rt, func, ID_EX_Rd, ID_EX_Rs, ID_EX_Rt, MEM_WB_Rd,
       multiplexer_2_out;
  wire [3:0] opcode;
  wire [11:0] main_5_imm_2, main_8_imm_2;
  wire [11:3] main_1_instruction;
  wire [15:0] adder_1_out, bit_extender_1_out, bit_extender_2_out, main_1_incremented_pc_2, main_4_out1,
       main_4_out2, main_5_incrementedpc_2, main_5_readreg1_2, main_5_readreg2_2, main_6_output,
       main_8_aluout_2, main_8_incrementedpc_2, main_8_memdata_2, main_9_aluresult_2, main_9_memreaddata_2,
       main_10_out, multiplexer_1_out, multiplexer_3_out, multiplexer_4_out, multiplexer_5_out,
       multiplexer_6_out, multiplexer_7_out, multiplexer_8_out, multiplexer_9_out,
       nextpc_1_jump_or_branch_target_address_16, PC_q, ram_1_data, ram_2_data;

  Multiplexer #(.width(16), .enable("false")) multiplexer_1 (
    .in0(adder_1_out), .in1(nextpc_1_jump_or_branch_target_address_16), .out(multiplexer_1_out), .sel(PcSrc));
  not not_1 (not_1_out, stall);
  Clock clock_1 (.out(clk));
  Register #(.width(16)) PC (.D(multiplexer_1_out), .en(not_1_out), .Q(PC_q), .clk(clk));  // open: clr
  Adder #(.width(16)) adder_1 (.a(16'h1), .b(PC_q), .out(adder_1_out));  // open: cin, cout
  not not_2 (not_2_out, stall);
  RAM #(.addrWidth(16), .dataWidth(16)) ram_1 (.addr(PC_q), .data(ram_1_data));  // open: sel, clk, ld, clr
  IF_IDBuffer_main main_1 (
    .Incremented_PC(adder_1_out), .Instuction(ram_1_data), .Incremented_PC_2(main_1_incremented_pc_2),
    .Instruction({opcode, main_1_instruction, func}), .Clk(clk), .in_4(not_2_out));
  regFile regfile_1 ();
  Multiplexer #(.width(3), .enable("false")) multiplexer_2 (
    .in0(main_1_instruction[8:6]), .in1(main_1_instruction[5:3]), .out(multiplexer_2_out), .sel(regDst));
  ControlUnit_main main_2 (
    .Opcode(opcode), .Func(func), .RegDst(regDst), .RegWrite(regWrite), .ALUSrc(AluSrc), .Beq(BEQ), .J(J),
    .JAL(JAL), .JR(JR), .AluOp(AluOp), .MemWrite(MemWrite), .MemRead(MemRead), .MemtoReg(MemToReg),
    .ExLb(extLb), .LworLb(LwOrLb), .storeReg(StoreReg));
  HazardUnit_main main_3 (
    .ID_EX_Memread(MemRead_EX), .ID_EX_RT(ID_EX_Rt), .IF_ID_RS(main_1_instruction[11:9]),
    .IF_ID_RT(main_1_instruction[8:6]), .Hazard(stall), .ID_EX_RT_2(ID_EX_Rt), .MemWrite(MemWrite));
  regFile_main main_4 (
    .WR_en(regWrite), .write_Reg(MEM_WB_Rd), .Write_Data(multiplexer_7_out), .reg1(main_1_instruction[11:9]),
    .reg2(main_1_instruction[8:6]), .CLK(clk), .OUT1(main_4_out1), .OUT2(main_4_out2));
  ID_EXBuffer_main main_5 (
    .IncrementedPC(main_1_incremented_pc_2), .IMM({main_1_instruction, func}), .MemtoReg(MemToReg),
    .RegWrite(regWrite), .RegDest(regDst), .ALUOp(AluOp), .ALUSrc(AluSrc), .JR(JR), .JAL(JAL), .J(J),
    .BEQ(BEQ), .extLB(extLb), .LwOrLb(LwOrLb), .StoreReg(StoreReg), .MemWrite(MemWrite), .MemRead(MemRead),
    .ReadReg1(main_4_out1), .ReadReg2(main_4_out2), .RS(main_1_instruction[11:9]),
    .RT(main_1_instruction[8:6]), .RD(multiplexer_2_out), .clk(clk),
    .IncrementedPC_2(main_5_incrementedpc_2), .IMM_2(main_5_imm_2), .MemtoReg_2(MemToReg_EX),
    .RegWrite_2(regWrite_EX), .RegDest_2(regDst_EX), .ALUOp_2(AluOpEX), .ALUSrc_2(AluSrcEX), .JR_2(JR_EX),
    .JAL_2(JAL_EX), .J_2(J_Ex), .BEQ_2(BEQ_EX), .extLB_2(extLb_EX), .LwOrLb_2(LwOrLb_EX),
    .StoreReg_2(StoreReg_EX), .MemWrite_2(MemWrite_EX), .MemRead_2(MemRead_EX),
    .ReadReg1_2(main_5_readreg1_2), .ReadReg2_2(main_5_readreg2_2), .Rs_2(ID_EX_Rs), .RT_2(ID_EX_Rt),
    .RD_2(ID_EX_Rd), .clr(undriven));
  assign bit_extender_1_out = {{10{1'b0}}, main_5_imm_2[5:0]};  // Bit_Extender bit_extender_1
  Multiplexer #(.select(2), .width(16), .enable("false")) multiplexer_3 (
    .in0(main_5_readreg2_2), .in1(multiplexer_7_out), .in2(main_8_aluout_2), .out(multiplexer_3_out),
    .sel(Forward_B));  // open: in3
  Multiplexer #(.select(2), .width(16), .enable("false")) multiplexer_4 (
    .in0(main_5_readreg1_2), .in1(multiplexer_7_out), .in2(main_8_aluout_2), .out(multiplexer_4_out),
    .sel(Forward_A));  // open: in3
  Multiplexer #(.width(16), .enable("false")) multiplexer_5 (
    .in0(multiplexer_3_out), .in1(bit_extender_1_out), .out(multiplexer_5_out), .sel(AluSrcEX));
  alu_main main_6 (
    .in_1(multiplexer_4_out), .in_2(multiplexer_5_out), .alu_operation(AluOpEX), .Output(main_6_output),
    .Zero_flag(Zero_EX), .Carry_out(carryOut), .alu_en(1'b1));
  forwarding_unit_main main_7 (
    .ID_EX_Rs(ID_EX_Rs), .EX_MEM_Rd(EX_MEM_Rd), .EX_MEM_RegWrite(regWrite_MEM), .ID_EX_Rt(ID_EX_Rt),
    .MEM_WB_Rd(MEM_WB_Rd), .MEM_WB_RegWrite(regWrite_WB), .Forward_A(Forward_A), .Forward_B(Forward_B));
  EX_MEMBuffer_main main_8 (
    .IncrementedPC(main_5_incrementedpc_2), .IMM(main_5_imm_2), .MemtoReg(MemToReg_EX),
    .RegWrite(regWrite_EX), .RegDest(regDst_EX), .JR(JR_EX), .AluOut(main_6_output), .zero(Zero_EX),
    .JAL(JAL_EX), .J(J_Ex), .BEQ(BEQ_EX), .extLB(extLb_EX), .LwOrLb(LwOrLb_EX), .StoreReg(StoreReg_EX),
    .MemWrite(MemWrite_EX), .MemRead(MemRead_EX), .RS(ID_EX_Rs), .RT(ID_EX_Rt), .RD(ID_EX_Rd), .clk(clk),
    .IncrementedPC_2(main_8_incrementedpc_2), .IMM_2(main_8_imm_2), .MemtoReg_2(MemToReg_MEM),
    .RegWrite_2(regWrite_MEM), .RegDest_2(regDst_MEM), .JR_2(JR_MEM), .AluOut_2(main_8_aluout_2),
    .zero_2(Zero_MEM), .JAL_2(JAL_MEM), .J_2(J_MEM), .BEQ_2(BEQ_MEM), .extLB_2(extLb_MEM),
    .LwOrLb_2(LwOrLb_MEM), .StoreReg_2(StoreReg_MEM), .MemWrite_2(MemWrite_MEM), .MemRead_2(MemRead_MEM),
    .Rs_2(EX_MEM_Rs), .RT_2(EX_MEM_Rt), .RD_2(EX_MEM_Rd), .memData(main_5_readreg2_2),
    .memData_2(main_8_memdata_2));
  NextPCdone_NextPC nextpc_1 (
    .Beq(BEQ_MEM), .J(J_MEM), .Zero(Zero_MEM), .PCSrc(PcSrc),
    .Jump_or_Branch_Target_Address_16(nextpc_1_jump_or_branch_target_address_16), .Imm_12(main_8_imm_2),
    .PC_16(main_8_incrementedpc_2), .JAL(JAL_MEM));
  assign bit_extender_2_out = {{8{1'b0}}, main_8_memdata_2[7:0]};  // Bit_Extender bit_extender_2
  Multiplexer #(.width(16), .enable("false")) multiplexer_6 (
    .in0(main_8_memdata_2), .in1(bit_extender_2_out), .out(multiplexer_6_out), .sel(StoreReg_MEM));
  Multiplexer #(.width(16), .enable("false")) multiplexer_7 (
    .in0(multiplexer_9_out), .in1(multiplexer_8_out), .out(multiplexer_7_out), .sel(MemToReg_WB));
  RAM #(.addrWidth(16), .dataWidth(16), .bus("separate")) ram_2 (
    .addr(main_8_aluout_2), .din(multiplexer_6_out), .data(ram_2_data), .str(MemWrite_MEM), .clk(clk),
    .ld(MemRead_MEM));  // open: sel, clr
  Multiplexer #(.width(16), .enable("false")) multiplexer_8 (
    .in0(multiplexer_9_out), .in1(main_10_out), .out(multiplexer_8_out), .sel(LwOrLb_WB));
  MEM_WB_main main_9 (
    .MemtoReg(MemToReg_MEM), .RegWrite(regWrite_MEM), .ALUresult(main_8_aluout_2), .MemReadData(ram_2_data),
    .LwOrLb(LwOrLb_MEM), .extLb(extLb_MEM), .clk(clk), .MemtoReg_2(MemToReg_WB), .RegWrite_2(regWrite_WB),
    .ALUresult_2(main_9_aluresult_2), .MemReadData_2(main_9_memreaddata_2), .LwOrLb_2(LwOrLb_WB),
    .extLb_2(extLb_WB), .WriteReg(EX_MEM_Rd), .WriteReg_2(MEM_WB_Rd));  // open: clear
  Extender8Bit_main main_10 (.Imm(multiplexer_9_out[7:0]), .Out(main_10_out), .ExtLb(extLb_WB));
  Multiplexer #(.width(16), .enable("false")) multiplexer_9 (
    .in0(main_9_aluresult_2), .in1(main_9_memreaddata_2), .out(multiplexer_9_out), .sel(MemToReg_WB));
  // AND_Gate and_1 is placed but not wired

  // Notes on the sheet:
  //   PC+1
endmodule
