// Logisim project DataPath123.circ as structural Verilog
module main (
);

  wire main_2_p1;
  wire [15:0] adder_1_out, undriven;

  Adder #(.width(16)) adder_1 (.a(16'h1), .b(undriven), .out(adder_1_out));  // open: cin, cout
  Multiplexer #(.width(16), .enable("false")) multiplexer_1 ();  // open: in0, in1, out, sel
  Register #(.width(16)) PC ();  // open: D, en, Q, clk, clr
  RAM #(.addrWidth(16), .dataWidth(16)) ram_1 ();  // open: addr, data, sel, clk, ld, clr
  // regFile_main main_1: pin names not known
  // NextPCdone_NextPC nextpc_1: pin names not known
  // alu_main main_2: pin names not known; wires that end beside it: main_2_p1, main_2_p1
  RAM #(.addrWidth(16), .dataWidth(16)) ram_2 ();  // open: addr, data, sel, clk, ld, clr
endmodule
