// Logisim project DataPath1234.circ as structural Verilog
module main (
);

  wire AluSrc, BEQ, carryOut, clk, extLb, J, JAL, JR, LwOrLb, MemRead, MemToReg, MemWrite, PcSrc, regDst,
       regWrite, StoreReg, Zero;
  wire [2:0] AluOp, func, multiplexer_3_out, ram_1_data_2;
  wire [3:0] opcode;
  wire [7:0] multiplexer_8_out;
  wire [9:4] ram_1_data;
  wire [15:0] adder_1_out, bit_extender_1_out, bit_extender_2_out, main_2_out1, main_2_out2, main_3_output,
       main_4_out, multiplexer_1_out, multiplexer_2_out, multiplexer_4_out, multiplexer_5_out,
       multiplexer_6_out, multiplexer_7_out, nextpc_1_jump_or_branch_target_address_16, PC_q, ram_2_data;
  wire [15:8] multiplexer_8_out_2;

  Multiplexer #(.width(16), .enable("false")) multiplexer_1 (
    .in0(adder_1_out), .in1(nextpc_1_jump_or_branch_target_address_16), .out(multiplexer_1_out), .sel(PcSrc));
  Clock clock_1 (.out(clk));
  Multiplexer #(.width(16), .enable("false")) multiplexer_2 (
    .in0(multiplexer_1_out), .in1(main_3_output), .out(multiplexer_2_out), .sel(JR));
  Register #(.width(16)) PC (.D(multiplexer_2_out), .Q(PC_q), .clk(clk));  // open: en, clr
  Adder #(.width(16)) adder_1 (.a(16'h1), .b(PC_q), .out(adder_1_out));  // open: cin, cout
  RAM #(.addrWidth(16), .dataWidth(16)) ram_1 (
    .addr(PC_q), .data({func, ram_1_data_2, ram_1_data, opcode}));  // open: sel, clk, ld, clr
  ControlUnit_main main_1 (
    .Opcode(opcode), .Func(func), .RegDst(regDst), .RegWrite(regWrite), .ALUSrc(AluSrc), .Beq(BEQ), .J(J),
    .JAL(JAL), .JR(JR), .AluOp(AluOp), .MemWrite(MemWrite), .MemRead(MemRead), .MemtoReg(MemToReg),
    .ExLb(extLb), .LworLb(LwOrLb), .storeReg(StoreReg));
  Multiplexer #(.width(3), .enable("false")) multiplexer_3 (
    .in0(ram_1_data[9:7]), .in1(ram_1_data_2), .out(multiplexer_3_out), .sel(regDst));
  regFile_main main_2 (
    .WR_en(regWrite), .write_Reg(multiplexer_3_out), .Write_Data(multiplexer_5_out), .reg1(ram_1_data[6:4]),
    .reg2(ram_1_data[9:7]), .CLK(clk), .OUT1(main_2_out1), .OUT2(main_2_out2));
  assign bit_extender_1_out = {{10{1'b0}}, {func, ram_1_data_2}};  // Bit_Extender bit_extender_1
  Multiplexer #(.width(16), .enable("false")) multiplexer_4 (
    .in0(main_2_out2), .in1(bit_extender_1_out), .out(multiplexer_4_out), .sel(AluSrc));
  NextPCdone_NextPC nextpc_1 (
    .Beq(BEQ), .J(J), .Zero(Zero), .PCSrc(PcSrc),
    .Jump_or_Branch_Target_Address_16(nextpc_1_jump_or_branch_target_address_16),
    .Imm_12({func, ram_1_data_2, ram_1_data}), .PC_16(adder_1_out), .JAL(JAL));
  alu_main main_3 (
    .in_1(main_2_out1), .in_2(multiplexer_4_out), .alu_operation(AluOp), .Output(main_3_output),
    .Zero_flag(Zero), .Carry_out(carryOut), .alu_en(1'b1));
  assign bit_extender_2_out = {{8{1'b0}}, main_2_out2[7:0]};  // Bit_Extender bit_extender_2
  Multiplexer #(.width(16), .enable("false")) multiplexer_5 (
    .in0({multiplexer_8_out_2, multiplexer_8_out}), .in1(multiplexer_7_out), .out(multiplexer_5_out),
    .sel(MemToReg));
  Multiplexer #(.width(16), .enable("false")) multiplexer_6 (
    .in0(main_2_out2), .in1(bit_extender_2_out), .out(multiplexer_6_out), .sel(StoreReg));
  RAM #(.addrWidth(16), .dataWidth(16), .bus("separate")) ram_2 (
    .addr(main_3_output), .din(multiplexer_6_out), .data(ram_2_data), .str(MemWrite), .clk(clk), .ld(MemRead));  // open: sel, clr
  Multiplexer #(.width(16), .enable("false")) multiplexer_7 (
    .in0({multiplexer_8_out_2, multiplexer_8_out}), .in1(main_4_out), .out(multiplexer_7_out), .sel(LwOrLb));
  Extender8Bit_main main_4 (.Imm(multiplexer_8_out), .Out(main_4_out), .ExtLb(extLb));
  Multiplexer #(.width(16), .enable("false")) multiplexer_8 (
    .in0(main_3_output), .in1(ram_2_data), .out({multiplexer_8_out_2, multiplexer_8_out}), .sel(MemToReg));
endmodule
