// Logisim project EX-MEMBuffer.circ as structural Verilog: 1 circuit, main circuit main
module main (
  input  [15:0] IncrementedPC,
  input  [11:0] IMM,
  input  MemtoReg,
  input  RegWrite,
  input  RegDest,
  input  JR,
  input  [15:0] AluOut,
  input  [15:0] memData,
  input  zero,
  input  JAL,
  input  J,
  input  BEQ,
  input  extLB,
  input  LwOrLb,
  input  StoreReg,
  input  MemWrite,
  input  MemRead,
  input  [2:0] RS,
  input  [2:0] RT,
  input  [2:0] RD,
  input  clk,
  output [15:0] IncrementedPC_2,
  output [11:0] IMM_2,
  output MemtoReg_2,
  output RegWrite_2,
  output RegDest_2,
  output JR_2,
  output [15:0] AluOut_2,
  output [15:0] memData_2,
  output zero_2,
  output JAL_2,
  output J_2,
  output BEQ_2,
  output extLB_2,
  output LwOrLb_2,
  output StoreReg_2,
  output MemWrite_2,
  output MemRead_2,
  output [2:0] Rs_2,
  output [2:0] RT_2,
  output [2:0] RD_2
);

  Register #(.width(16)) Incremented_PC (.D(IncrementedPC), .Q(IncrementedPC_2), .clk(clk));  // open: en, clr
  Register #(.width(12)) SignExtendOffset (.D(IMM), .Q(IMM_2), .clk(clk));  // open: en, clr
  Register #(.width(1)) WriteBack (.D(MemtoReg), .Q(MemtoReg_2), .clk(clk));  // open: en, clr
  Register #(.width(1)) WriteBack_2 (.D(RegWrite), .Q(RegWrite_2), .clk(clk));  // open: en, clr
  Register #(.width(1)) Execute (.D(RegDest), .Q(RegDest_2), .clk(clk));  // open: en, clr
  Register #(.width(1)) Execute_2 (.D(JR), .Q(JR_2), .clk(clk));  // open: en, clr
  Register #(.width(16)) u_AluOut (.D(AluOut), .Q(AluOut_2), .clk(clk));  // open: en, clr
  Register #(.width(16)) u_memData (.D(memData), .Q(memData_2), .clk(clk));  // open: en, clr
  Register #(.width(1)) u_zero (.D(zero), .Q(zero_2), .clk(clk));  // open: en, clr
  Register #(.width(1)) Execute_3 (.D(JAL), .Q(JAL_2), .clk(clk));  // open: en, clr
  Register #(.width(1)) Execute_4 (.D(J), .Q(J_2), .clk(clk));  // open: en, clr
  Register #(.width(1)) Mem (.D(BEQ), .Q(BEQ_2), .clk(clk));  // open: en, clr
  Register #(.width(1)) Mem_2 (.D(extLB), .Q(extLB_2), .clk(clk));  // open: en, clr
  Register #(.width(1)) Mem_3 (.D(LwOrLb), .Q(LwOrLb_2), .clk(clk));  // open: en, clr
  Register #(.width(1)) Mem_4 (.D(StoreReg), .Q(StoreReg_2), .clk(clk));  // open: en, clr
  Register #(.width(1)) Mem_5 (.D(MemWrite), .Q(MemWrite_2), .clk(clk));  // open: en, clr
  Register #(.width(1)) Mem_6 (.D(MemRead), .Q(MemRead_2), .clk(clk));  // open: en, clr
  Register #(.width(3)) u_RS (.D(RS), .Q(Rs_2), .clk(clk));  // open: en, clr
  Register #(.width(3)) u_RT (.D(RT), .Q(RT_2), .clk(clk));  // open: en, clr
  Register #(.width(3)) u_RD (.D(RD), .Q(RD_2), .clk(clk));  // open: en, clr
endmodule
