// Logisim project Extender8Bit.circ as structural Verilog: 1 circuit, main circuit main
module main (
  input  [7:0] Imm,
  input  ExtLb,
  output [15:0] Out
);

  wire [15:0] bit_extender_1_out, bit_extender_2_out;

  assign bit_extender_1_out = {{8{1'b0}}, Imm};  // Bit_Extender bit_extender_1
  assign bit_extender_2_out = {{8{Imm[7]}}, Imm};  // Bit_Extender bit_extender_2
  Multiplexer #(.width(16), .enable("false")) multiplexer_1 (
    .in0(bit_extender_1_out), .in1(bit_extender_2_out), .out(Out), .sel(ExtLb));
endmodule
