// Logisim project HazardUnit.circ as structural Verilog: 1 circuit, main circuit main
module main (
  input  ID_EX_Memread,
  input  MemWrite,
  input  [2:0] ID_EX_RT,
  input  [2:0] IF_ID_RS,
  input  [2:0] IF_ID_RT,
  input  [2:0] ID_EX_RT_2,
  output Hazard
);

  wire and_1_out, comparator_1_eq, comparator_2_eq, comparator_3_eq, not_1_out, or_1_out;

  Comparator #(.width(3), .mode("unsigned")) comparator_1 (
    .a(ID_EX_RT), .b(IF_ID_RS), .eq(comparator_1_eq));  // open: gt, lt
  Comparator #(.width(3), .mode("unsigned")) comparator_2 (
    .a(ID_EX_RT), .b(IF_ID_RT), .eq(comparator_2_eq));  // open: gt, lt
  and and_1 (and_1_out, ~MemWrite, comparator_2_eq);  // AND_Gate
  or or_1 (or_1_out, and_1_out, comparator_1_eq);
  Comparator #(.width(3)) comparator_3 (.a(ID_EX_RT_2), .b(3'b000), .eq(comparator_3_eq));  // open: gt, lt
  not not_1 (not_1_out, comparator_3_eq);
  and and_2 (Hazard, ID_EX_Memread, or_1_out, not_1_out);
endmodule
