// Logisim project ID-EXBuffer.circ as structural Verilog: 1 circuit, main circuit main
module main (
  input  [15:0] IncrementedPC,
  input  [11:0] IMM,
  input  MemtoReg,
  input  RegWrite,
  input  RegDest,
  input  [2:0] ALUOp,
  input  ALUSrc,
  input  JR,
  input  [15:0] ReadReg1,
  input  [15:0] ReadReg2,
  input  JAL,
  input  J,
  input  BEQ,
  input  extLB,
  input  LwOrLb,
  input  StoreReg,
  input  MemWrite,
  input  MemRead,
  input  [2:0] RS,
  input  [2:0] RT,
  input  [2:0] RD,
  input  clk,
  input  clr,
  output [15:0] IncrementedPC_2,
  output [11:0] IMM_2,
  output MemtoReg_2,
  output RegWrite_2,
  output RegDest_2,
  output [2:0] ALUOp_2,
  output ALUSrc_2,
  output JR_2,
  output [15:0] ReadReg1_2,
  output [15:0] ReadReg2_2,
  output JAL_2,
  output J_2,
  output BEQ_2,
  output extLB_2,
  output LwOrLb_2,
  output StoreReg_2,
  output MemWrite_2,
  output MemRead_2,
  output [2:0] Rs_2,
  output [2:0] RT_2,
  output [2:0] RD_2
);

  wire undriven;

  Register #(.width(16)) Incremented_PC (.D(IncrementedPC), .en(clr), .Q(IncrementedPC_2), .clk(clk));  // open: clr
  Register #(.width(12)) SignExtendOffset (.D(IMM), .en(clr), .Q(IMM_2), .clk(clk));  // open: clr
  Register #(.width(1)) WriteBack (.D(MemtoReg), .en(clr), .Q(MemtoReg_2), .clk(clk));  // open: clr
  Register #(.width(1)) WriteBack_2 (.D(RegWrite), .en(clr), .Q(RegWrite_2), .clk(clk));  // open: clr
  Register #(.width(1)) Execute (.D(RegDest), .en(clr), .Q(RegDest_2), .clk(clk));  // open: clr
  Register #(.width(3)) Execute_2 (.D(ALUOp), .en(clr), .Q(ALUOp_2), .clk(clk));  // open: clr
  Register #(.width(1)) Execute_3 (.D(ALUSrc), .en(clr), .Q(ALUSrc_2), .clk(clk));  // open: clr
  Register #(.width(1)) Execute_4 (.D(JR), .en(clr), .Q(JR_2), .clk(clk));  // open: clr
  Register #(.width(16)) u_ReadReg1 (.D(ReadReg1), .en(clr), .Q(ReadReg1_2), .clk(clk));  // open: clr
  Register #(.width(16)) u_ReadReg2 (.D(ReadReg2), .en(clr), .Q(ReadReg2_2), .clk(clk));  // open: clr
  Register #(.width(1)) Execute_5 (.D(JAL), .en(clr), .Q(JAL_2), .clk(clk));  // open: clr
  Register #(.width(1)) Execute_6 (.D(J), .en(clr), .Q(J_2), .clk(clk));  // open: clr
  Register #(.width(1)) Mem (.D(BEQ), .en(clr), .Q(BEQ_2), .clk(clk));  // open: clr
  Register #(.width(1)) Mem_2 (.D(extLB), .en(clr), .Q(extLB_2), .clk(clk));  // open: clr
  Register #(.width(1)) Mem_3 (.D(LwOrLb), .en(clr), .Q(LwOrLb_2), .clk(clk), .clr(undriven));
  Register #(.width(1)) Mem_4 (.D(StoreReg), .Q(StoreReg_2), .clk(clk), .clr(clr));  // open: en
  Register #(.width(1)) Mem_5 (.D(MemWrite), .en(clr), .Q(MemWrite_2), .clk(clk));  // open: clr
  Register #(.width(1)) Mem_6 (.D(MemRead), .en(clr), .Q(MemRead_2), .clk(clk));  // open: clr
  Register #(.width(3)) u_RS (.D(RS), .en(clr), .Q(Rs_2), .clk(clk));  // open: clr
  Register #(.width(3)) u_RT (.D(RT), .en(clr), .Q(RT_2), .clk(clk));  // open: clr
  Register #(.width(3)) u_RD (.D(RD), .en(clr), .Q(RD_2), .clk(clk));  // open: clr
endmodule
