// Logisim project IF-IDBuffer.circ as structural Verilog: 1 circuit, main circuit main
module main (
  input  [15:0] Incremented_PC,
  input  [15:0] Instuction,
  input  Clk,
  input  in_4,
  output [15:0] Incremented_PC_2,
  output [15:0] Instruction
);

  Register #(.width(16)) u_Incremented_PC (
    .D(Incremented_PC), .en(in_4), .Q(Incremented_PC_2), .clk(Clk));  // open: clr
  Register #(.width(16)) u_Instruction (.D(Instuction), .en(in_4), .Q(Instruction), .clk(Clk));  // open: clr
endmodule
