// Logisim project MEM-WB.circ as structural Verilog: 1 circuit, main circuit main
module main (
  input  MemtoReg,
  input  RegWrite,
  input  [15:0] ALUresult,
  input  [15:0] MemReadData,
  input  LwOrLb,
  input  extLb,
  input  [2:0] WriteReg,
  input  clk,
  input  clear,
  output MemtoReg_2,
  output RegWrite_2,
  output [15:0] ALUresult_2,
  output [15:0] MemReadData_2,
  output LwOrLb_2,
  output extLb_2,
  output [2:0] WriteReg_2
);

  Register #(.width(1)) WriteBack (.D(MemtoReg), .Q(MemtoReg_2), .clk(clk), .clr(clear));  // open: en
  Register #(.width(1)) WriteBack_2 (.D(RegWrite), .Q(RegWrite_2), .clk(clk), .clr(clear));  // open: en
  Register #(.width(16)) u_ALUresult (.D(ALUresult), .Q(ALUresult_2), .clk(clk), .clr(clear));  // open: en
  Register #(.width(16)) u_MemReadData (.D(MemReadData), .Q(MemReadData_2), .clk(clk), .clr(clear));  // open: en
  Register #(.width(1)) u_LwOrLb (.D(LwOrLb), .Q(LwOrLb_2), .clk(clk), .clr(clear));  // open: en
  Register #(.width(1)) u_extLb (.D(extLb), .Q(extLb_2), .clk(clk), .clr(clear));  // open: en
  Register #(.width(3)) RT (.D(WriteReg), .Q(WriteReg_2), .clk(clk), .clr(clear));  // open: en
endmodule
