// Logisim project NextPCdone.circ as structural Verilog: 2 circuits, main circuit NextPC
module NextPC (
  input  [15:0] PC_16,
  input  Beq,
  input  Zero,
  input  J,
  input  JAL,
  input  [11:0] Imm_12,
  output PCSrc,
  output [15:0] Jump_or_Branch_Target_Address_16
);

  wire and_1_out, or_1_out;
  wire [15:0] adder_1_out, adder_2_out, bit_extender_1_out, bit_extender_2_out;

  assign bit_extender_1_out = {{10{Imm_12[5]}}, Imm_12[5:0]};  // Bit_Extender bit_extender_1
  assign bit_extender_2_out = {{4{Imm_12[11]}}, Imm_12};  // Bit_Extender bit_extender_2
  Adder #(.width(16)) adder_1 (.a(PC_16), .b(bit_extender_1_out), .out(adder_1_out));  // open: cin, cout
  Adder #(.width(16)) adder_2 (.a(PC_16), .b(bit_extender_2_out), .out(adder_2_out));  // open: cin, cout
  Multiplexer #(.width(16), .enable("false")) multiplexer_1 (
    .in0(adder_1_out), .in1(adder_2_out), .out(Jump_or_Branch_Target_Address_16), .sel(or_1_out));
  or or_1 (or_1_out, J, JAL);
  or or_2 (PCSrc, J, JAL, and_1_out);
  and and_1 (and_1_out, Zero, Beq);
endmodule

module test (
  input  in_1,
  input  in_2,
  input  in_3,
  input  in_4,
  output [31:0] out_5,
  output out_6
);

  // NextPC nextpc_1: pin names not known; wires that end beside it: out_5, in_4, out_6
endmodule
