// Logisim project forwarding_unit.circ as structural Verilog: 1 circuit, main circuit main
module main (
  input  [2:0] ID_EX_Rs,
  input  [2:0] EX_MEM_Rd,
  input  EX_MEM_RegWrite,
  input  [2:0] ID_EX_Rt,
  input  [2:0] MEM_WB_Rd,
  input  MEM_WB_RegWrite,
  output [1:0] Forward_A,
  output [1:0] Forward_B
);

  wire and_3_out, and_4_out, comparator_1_eq, comparator_2_eq, comparator_3_eq, comparator_4_eq;

  Comparator #(.width(3)) comparator_1 (.a(ID_EX_Rs), .b(EX_MEM_Rd), .eq(comparator_1_eq));  // open: gt, lt
  Comparator #(.width(3)) comparator_2 (.a(EX_MEM_Rd), .b(ID_EX_Rt), .eq(comparator_2_eq));  // open: gt, lt
  Comparator #(.width(3)) comparator_3 (.a(ID_EX_Rt), .b(MEM_WB_Rd), .eq(comparator_3_eq));  // open: gt, lt
  Comparator #(.width(3)) comparator_4 (.a(MEM_WB_Rd), .b(ID_EX_Rs), .eq(comparator_4_eq));  // open: gt, lt
  and and_1 (Forward_A[1], comparator_1_eq, EX_MEM_RegWrite);
  and and_2 (Forward_B[1], EX_MEM_RegWrite, comparator_2_eq);
  and and_3 (and_3_out, comparator_3_eq, MEM_WB_RegWrite);
  and and_4 (and_4_out, MEM_WB_RegWrite, comparator_4_eq);
  and and_5 (Forward_A[0], ~Forward_A[1], and_4_out);  // AND_Gate
  and and_6 (Forward_B[0], ~Forward_B[1], and_3_out);  // AND_Gate
endmodule
